// Logisim project 1part.circ as structural Verilog: 3 circuits, main circuit 2part
module main (
  input  x1,
  input  x2,
  input  x3,
  output P,
  output S
);

  wire not_1_out, not_2_out, not_3_out, or_1_out, or_2_out, or_3_out, or_4_out, or_5_out, or_6_out, or_7_out;

  not not_1 (not_1_out, x1);
  not not_2 (not_2_out, x2);
  not not_3 (not_3_out, x3);
  or or_1 (or_1_out, x1, x2);
  or or_2 (or_2_out, x1, x3);
  or or_3 (or_3_out, x2, x3);
  or or_4 (or_4_out, x1, x2, x3);
  or or_5 (or_5_out, x1, not_2_out, not_3_out);
  or or_6 (or_6_out, not_1_out, not_2_out, x3);
  or or_7 (or_7_out, not_1_out, x2, not_3_out);
  and and_1 (S, or_4_out, or_5_out, or_6_out, or_7_out);
  and and_2 (P, or_1_out, or_2_out, or_3_out);

  // Notes on the sheet:
  //   x1
  //   x2
  //   x3
  //   !x1
  //   !x2
  //   !x3
endmodule

module _2part (
  input  [7:0] in_1,
  input  in_2,
  input  [7:0] in_3,
  output [7:0] out_4
);

  wire main_1_p, main_2_p, main_3_p, main_4_p, main_5_p, main_6_p, main_7_p;

  // Probe on in_1
  // Probe on in_3
  main main_1 (.x1(in_1[0]), .x2(in_3[0]), .x3(in_2), .P(main_1_p), .S(out_4[0]));
  main main_2 (.x1(in_1[1]), .x2(in_3[1]), .x3(main_1_p), .P(main_2_p), .S(out_4[1]));
  main main_3 (.x1(in_1[2]), .x2(in_3[2]), .x3(main_2_p), .P(main_3_p), .S(out_4[2]));
  main main_4 (.x1(in_1[3]), .x2(in_3[3]), .x3(main_3_p), .P(main_4_p), .S(out_4[3]));
  main main_5 (.x1(in_1[4]), .x2(in_3[4]), .x3(main_4_p), .P(main_5_p), .S(out_4[4]));
  main main_6 (.x1(in_1[5]), .x2(in_3[5]), .x3(main_5_p), .P(main_6_p), .S(out_4[5]));
  main main_7 (.x1(in_1[6]), .x2(in_3[6]), .x3(main_6_p), .P(main_7_p), .S(out_4[6]));
  main main_8 (.x1(in_1[7]), .x2(in_3[7]), .x3(main_7_p), .S(out_4[7]));  // open: P
  // Probe on out_4
endmodule

module d8421 (
  input  x4,
  input  x3,
  input  x2,
  input  x1,
  output y4,
  output y3,
  output y2,
  output out_8
);

  wire not_1_out, not_2_out, not_3_out, not_4_out, or_1_out, or_2_out, or_3_out, or_4_out, or_5_out,
       or_6_out, or_7_out, or_8_out, or_9_out;

  not not_1 (not_1_out, x4);
  not not_2 (not_2_out, x3);
  not not_3 (not_3_out, x2);
  not not_4 (not_4_out, x1);
  or or_1 (or_1_out, not_1_out, x3, x2);
  or or_2 (or_2_out, x4, not_2_out, not_3_out, not_4_out);
  or or_3 (or_3_out, x3, x2);
  or or_4 (or_4_out, x4, not_2_out, not_3_out, not_4_out);
  or or_5 (or_5_out, x4, x2, x1);
  or or_6 (or_6_out, x4, not_3_out, not_4_out);
  or or_7 (or_7_out, not_1_out, x3, x2);
  or or_8 (or_8_out, x4, not_4_out);
  or or_9 (or_9_out, not_1_out, x3, x2);
  and and_1 (y4, or_1_out, or_2_out);
  and and_2 (y3, or_3_out, or_4_out);
  and and_3 (y2, or_5_out, or_6_out, or_7_out);
  and and_4 (out_8, or_8_out, or_9_out);

  // Notes on the sheet:
  //   x4
  //   x3
  //   x2
  //   x1
  //   !x4
  //   !x3
  //   !x2
  //   !x1
  //   y1
endmodule
