// Logisim project 2part.circ as structural Verilog: 1 circuit, main circuit main
module main (
  input  [7:0] in_1,
  input  in_2,
  input  [7:0] in_3
);

  // Probe on in_1
  // Probe on in_3
endmodule
